// Logisim project cpu_new.circ as structural Verilog: 12 circuits, main circuit main
module main (
  input  reset,
  output [31:0] Instr,
  output [31:0] PC,
  output RegWrite,
  output [4:0] RegAddr,
  output [31:0] RegData,
  output MemWrite,
  output [31:0] MemAddr,
  output [31:0] Memdata
);

  wire ALUsel, clk, EXTop, LessZero, Zero;
  wire [1:0] DMop, SelWd, SelWr;
  wire [2:0] NPCop;
  wire [3:0] ALUop;
  wire [4:0] _15_11, _20_16, _25_21;
  wire [5:0] funct, opcode;
  wire [15:0] Imm16;
  wire [25:0] Imm26;
  wire [31:0] EXT_IMM, multiplexer_3_out, PC_4, RA, RD;

  Clock clock_1 (.out(clk));
  Splitter splitter_1 (
    .Code(Instr), .funct(funct), ._15_11(_15_11), ._20_16(_20_16), ._25_21(_25_21), .opcode(opcode),
    .Imm26(Imm26), .Imm16(Imm16));
  IFU ifu_1 (
    .Imm(Imm26), .Zero(Zero), .clk(clk), .reset(reset), .Ra(RA), .NPCop(NPCop), .PC_4(PC_4), .Instr(Instr),
    .PC(PC));
  Controller controller_1 (
    .funct(funct), .opcode(opcode), .ALUsel(ALUsel), .ALUop(ALUop), .DMwr(MemWrite), .SelWr(SelWr),
    .NPCop(NPCop), .SelWd(SelWd), .WE(RegWrite), .EXTop(EXTop), .DMop(DMop));
  Multiplexer #(.select(2), .width(5)) multiplexer_1 (
    .in0(_15_11), .in1(_20_16), .in2({5{1'b1}}), .out(RegAddr), .sel(SelWr));  // open: in3, en
  Multiplexer #(.select(2), .width(32)) multiplexer_2 (
    .in0(RD), .in1(MemAddr), .in2(PC_4), .out(RegData), .sel(SelWd));  // open: in3, en
  GRF grf_1 (
    .clk(clk), .reset(reset), .\WE使能 (RegWrite), .A1(_25_21), .A2(_20_16), .A3(RegAddr), .WD(RegData),
    .RD1(RA), .RD2(Memdata));
  // Probe on MemAddr
  Multiplexer #(.width(32)) multiplexer_3 (
    .in0(Memdata), .in1(EXT_IMM), .out(multiplexer_3_out), .sel(ALUsel));  // open: en
  EXT ext_1 (.Imm(Imm16), .EXTop(EXTop), .extOut(EXT_IMM));
  ALU alu_1 (.ALUop(ALUop), .A(RA), .B(multiplexer_3_out), .Zero(Zero), .LessZero(LessZero), .C(MemAddr));
  DM dm_1 (.addr(MemAddr), .DMwr(MemWrite), .WD(Memdata), .DMop(DMop), .RD(RD), .clk(clk), .reset(reset));
  // Probe on RD

  // Other names for the same wires on the sheet: DMwr = MemWrite; RD1[31:0] = RA; RD2[31:0] = Memdata;
  //   resultALU[31:0] = MemAddr; WE = RegWrite

  // Notes on the sheet:
  //   万能分线器-将IFU输出的指令进行分解，进一步传递给GRF/CTL
  //   IFU模块-取指令模块
  //   CTL-中央处理模块，对各个模块给出控制信号
  //   根据控制信号确定，要存入的寄存器的地址
  //   GRF模块-寄存器堆，功能是寄存器的读写，结果传给ALU处理
  //   根据控制信号确定，输入寄存器的数据来自DM/ALU/PC+4
  //   根据控制信号确定B来自哪里
  //   立即数扩展
  //   DM模块-数据存储器-进行内存memory的读写
  //   ALU模块-进行操作的各种计算
endmodule

module IFU (
  input  [25:0] Imm,
  input  Zero,
  input  clk,
  input  reset,
  input  [31:0] Ra,
  input  [2:0] NPCop,
  output [31:0] PC_4,
  output [31:0] PC,
  output [31:0] Instr
);

  wire comparator_1_eq;
  wire [31:0] adder_1_out, npc_1_npc, PC_q;

  NPC npc_1 (.PC(PC), .Imm(Imm), .Zero(Zero), .Ra(Ra), .NPCop(NPCop), .PC_4(PC_4), .NPC(npc_1_npc));
  // Probe on npc_1_npc
  Register #(.width(32)) u_PC (.D(npc_1_npc), .Q(PC_q), .clk(clk), .clr(reset));  // open: en
  // Probe on PC_q
  Comparator #(.width(32)) comparator_1 (.a({32{1'b0}}), .b(PC_q), .eq(comparator_1_eq));  // open: gt, lt
  Adder #(.width(32)) adder_1 (.a(PC_q), .b(32'h3000), .out(adder_1_out));  // open: cin, cout
  Multiplexer #(.width(32)) multiplexer_1 (.in0(PC_q), .in1(adder_1_out), .out(PC), .sel(comparator_1_eq));  // open: en
  // Probe on PC
  IM im_1 (.NPC(PC), .Instr(Instr));
endmodule

module IM (
  input  [31:0] NPC,
  output [31:0] Instr
);

  wire [31:0] subtractor_1_out;

  Subtractor #(.width(32)) subtractor_1 (.a(NPC), .b(32'h3000), .out(subtractor_1_out));  // open: bin, bout
  ROM #(.addrWidth(12), .dataWidth(32)) rom_1 (.addr(subtractor_1_out[13:2]), .data(Instr));  // open: sel

  // Notes on the sheet:
  //   contents of rom_1 (hex, n*v repeats v):
  //   35080005 ac080004 8c040004
endmodule

module NPC (
  input  [31:0] PC,
  input  [25:0] Imm,
  input  Zero,
  input  [31:0] Ra,
  input  [2:0] NPCop,
  output [31:0] PC_4,
  output [31:0] NPC
);

  wire [31:0] adder_2_out, bit_extender_1_out, multiplexer_1_out;

  // Probe on Imm[15:0]
  Adder #(.width(32)) adder_1 (.a(32'h4), .b(PC), .out(PC_4));  // open: cin, cout
  assign bit_extender_1_out = {{14{Imm[15]}}, {Imm[15:0], 2'b00}};  // Bit_Extender bit_extender_1
  Adder #(.width(32)) adder_2 (.a(PC_4), .b(bit_extender_1_out), .out(adder_2_out));  // open: cin, cout
  Multiplexer #(.width(32)) multiplexer_1 (
    .in0(PC_4), .in1(adder_2_out), .out(multiplexer_1_out), .sel(Zero));  // open: en
  Multiplexer #(.select(3), .width(32)) multiplexer_2 (
    .in0(PC_4), .in1(multiplexer_1_out), .in2({PC[31:28], Imm, 2'b00}), .in3(Ra), .out(NPC), .sel(NPCop));  // open: in4, in5, in6, in7, en

  // Notes on the sheet:
  //   PC+4
  //   beq
  //   jr
  //   j/jal
endmodule

// CTL
module Controller (
  input  [5:0] funct,
  input  [5:0] opcode,
  output ALUsel,
  output [3:0] ALUop,
  output DMwr,
  output [1:0] SelWr,
  output [2:0] NPCop,
  output [1:0] SelWd,
  output WE,
  output EXTop,
  output [1:0] DMop
);

  wire and_1_add, and_1_beq, and_1_j, and_1_jal, and_1_jr, and_1_lh, and_1_lui, and_1_lw, and_1_ori,
       and_1_sub, and_1_sw;

  AND and_1 (
    .JR(and_1_jr), .ADD(and_1_add), .SUB(and_1_sub), .ORI(and_1_ori), .LW(and_1_lw), .SW(and_1_sw),
    .BEQ(and_1_beq), .LUI(and_1_lui), .J(and_1_j), .JAL(and_1_jal), .opcode(opcode), .funct(funct),
    .LH(and_1_lh));
  OR or_1 (
    .ADD(and_1_add), .JAL(and_1_jal), .SUB(and_1_sub), .ORI(and_1_ori), .LW(and_1_lw), .SW(and_1_sw),
    .BEQ(and_1_beq), .LUI(and_1_lui), .J(and_1_j), .ALUsel(ALUsel), .ALUop(ALUop), .DMwr(DMwr),
    .SelWr(SelWr), .NPCop(NPCop), .SelWd(SelWd), .WE(WE), .EXTop(EXTop), .JR(and_1_jr), .LH(and_1_lh),
    .DMop(DMop));
endmodule

module AND (
  input  [5:0] opcode,
  input  [5:0] funct,
  output JR,
  output ADD,
  output SUB,
  output ORI,
  output LW,
  output SW,
  output BEQ,
  output LUI,
  output J,
  output JAL,
  output LH
);

  wire add_out, jr_out, not_1_out, not_2_out, not_3_out, not_4_out, not_5_out, not_6_out, not_7_out,
       not_8_out, not_9_out, not_10_out, not_11_out, not_12_out, special_out, sub_out;

  not not_1 (not_1_out, opcode[5]);
  not not_2 (not_2_out, opcode[4]);
  not not_3 (not_3_out, funct[5]);
  not not_4 (not_4_out, funct[4]);
  not not_5 (not_5_out, opcode[3]);
  not not_6 (not_6_out, funct[3]);
  not not_7 (not_7_out, opcode[2]);
  not not_8 (not_8_out, funct[2]);
  not not_9 (not_9_out, opcode[1]);
  not not_10 (not_10_out, funct[1]);
  not not_11 (not_11_out, opcode[0]);
  not not_12 (not_12_out, funct[0]);
  and special (special_out, not_1_out, not_2_out, not_5_out, not_7_out, not_9_out, not_11_out);
  and u_ori (ORI, not_1_out, not_2_out, opcode[3], opcode[2], not_9_out, opcode[0]);
  and u_lw (LW, opcode[5], not_2_out, not_5_out, not_7_out, opcode[1], opcode[0]);
  and u_sw (SW, opcode[5], not_2_out, opcode[3], not_7_out, opcode[1], opcode[0]);
  and u_beq (BEQ, not_1_out, not_2_out, not_5_out, opcode[2], not_9_out, not_11_out);
  and u_lui (LUI, not_1_out, not_2_out, opcode[3], opcode[2], opcode[1], opcode[0]);
  and u_j (J, not_1_out, not_2_out, not_5_out, not_7_out, opcode[1], not_11_out);
  and u_jal (JAL, not_1_out, not_2_out, not_5_out, not_7_out, opcode[1], opcode[0]);
  and u_lh (LH, opcode[5], not_2_out, not_5_out, not_7_out, not_9_out, opcode[0]);
  and u_add (add_out, funct[5], not_4_out, not_6_out, not_8_out, not_10_out, not_12_out);
  and u_sub (sub_out, funct[5], not_4_out, not_6_out, not_8_out, funct[1], not_12_out);
  and u_jr (jr_out, not_3_out, not_4_out, funct[3], not_8_out, not_10_out, not_12_out);
  and ADD_2 (ADD, special_out, add_out);
  and SUB_2 (SUB, special_out, sub_out);
  and JR_2 (JR, special_out, jr_out);
endmodule

module OR (
  input  ADD,
  input  JAL,
  input  JR,
  input  SUB,
  input  LH,
  input  ORI,
  input  LW,
  input  SW,
  input  BEQ,
  input  LUI,
  input  J,
  output ALUsel,
  output [3:0] ALUop,
  output [2:0] NPCop,
  output DMwr,
  output [1:0] SelWr,
  output [1:0] SelWd,
  output WE,
  output EXTop,
  output [1:0] DMop
);

  wire or_1_out, pull_resistor_1_node;

  or or_1 (or_1_out, J, JAL);
  or or_2 (NPCop[0], pull_resistor_1_node, BEQ);
  or or_3 (NPCop[1], pull_resistor_1_node, or_1_out, JR);
  or or_4 (NPCop[2], JR, pull_resistor_1_node);
  Pull_Resistor pull_resistor_1 (.node(pull_resistor_1_node));
  or or_5 (EXTop, pull_resistor_1_node, SW, LW, LH);
  or or_6 (DMop[0], pull_resistor_1_node, LH);
  buf or_7 (DMop[1], pull_resistor_1_node);  // OR_Gate
  or or_8 (ALUop[0], pull_resistor_1_node, SUB, LUI);
  or or_9 (ALUop[1], pull_resistor_1_node, ORI, LUI);
  buf or_10 (ALUop[2], pull_resistor_1_node);  // OR_Gate
  buf or_11 (ALUop[3], pull_resistor_1_node);  // OR_Gate
  or or_12 (SelWr[0], LW, LH, ORI, LUI, pull_resistor_1_node);
  or or_13 (SelWr[1], JAL, pull_resistor_1_node);
  or or_14 (SelWd[1], JAL, pull_resistor_1_node);
  or or_15 (ALUsel, LW, pull_resistor_1_node, ORI, SW, LUI, LH);
  or or_16 (SelWd[0], ADD, SUB, ORI, LUI, pull_resistor_1_node);
  or or_17 (WE, LH, ADD, SUB, ORI, LW, LUI, JAL, pull_resistor_1_node);

  assign DMwr = SW;

  // Notes on the sheet:
  //   待进行jal/jr/j的拓展
endmodule

module GRF (
  input  clk,
  input  reset,
  input  \WE使能 ,
  input  [4:0] A1,
  input  [4:0] A2,
  input  [4:0] A3,
  input  [31:0] WD,
  output [31:0] RD1,
  output [31:0] RD2
);

  wire _0, _1, _2, _3, _4, _5, _6, _7, _8, _9, _10, _11, _12, _13, _14, _15, _16, _17, _18, _19, _20, _21,
       _22, _23, _24, _25, _26, _27, _28, _29, _30, _31;
  wire [31:0] _0out, _1out, _2out, _3out, _4out, _5out, _6out, _7out, _8out, _9out, _10out, _11out, _12out,
       _13out, _14out, _15out, _16out, _17out, _18out, _19out, _20out, _21out, _22out, _23out, _24out,
       _25out, _26out, _27out, _28out, _29out, _30out, _31out;

  Demultiplexer #(.select(5)) demultiplexer_1 (
    .out0(_0), .out1(_1), .out2(_2), .out3(_3), .out4(_4), .out5(_5), .out6(_6), .out7(_7), .out8(_8),
    .out9(_9), .out10(_10), .out11(_11), .out12(_12), .out13(_13), .out14(_14), .out15(_15), .out16(_16),
    .out17(_17), .out18(_18), .out19(_19), .out20(_20), .out21(_21), .out22(_22), .out23(_23), .out24(_24),
    .out25(_25), .out26(_26), .out27(_27), .out28(_28), .out29(_29), .out30(_30), .out31(_31), .in(\WE使能 ),
    .sel(A3));  // open: en
  Register #(.width(32)) register_1 (.D({32{1'b0}}), .en(_0), .Q(_0out), .clk(clk), .clr(reset));
  Register #(.width(32)) register_2 (.D(WD), .en(_6), .Q(_6out), .clk(clk), .clr(reset));
  Register #(.width(32)) register_3 (.D(WD), .en(_7), .Q(_7out), .clk(clk), .clr(reset));
  Register #(.width(32)) register_4 (.D(WD), .en(_13), .Q(_13out), .clk(clk), .clr(reset));
  Register #(.width(32)) register_5 (.D(WD), .en(_12), .Q(_12out), .clk(clk), .clr(reset));
  Register #(.width(32)) register_6 (.D(WD), .en(_18), .Q(_18out), .clk(clk), .clr(reset));
  Register #(.width(32)) register_7 (.D(WD), .en(_24), .Q(_24out), .clk(clk), .clr(reset));
  Register #(.width(32)) register_8 (.D(WD), .en(_30), .Q(_30out), .clk(clk), .clr(reset));
  Register #(.width(32)) register_9 (.D(WD), .en(_1), .Q(_1out), .clk(clk), .clr(reset));
  Register #(.width(32)) register_10 (.D(WD), .en(_8), .Q(_8out), .clk(clk), .clr(reset));
  Register #(.width(32)) register_11 (.D(WD), .en(_14), .Q(_14out), .clk(clk), .clr(reset));
  Register #(.width(32)) register_12 (.D(WD), .en(_19), .Q(_19out), .clk(clk), .clr(reset));
  Register #(.width(32)) register_13 (.D(WD), .en(_20), .Q(_20out), .clk(clk), .clr(reset));
  Register #(.width(32)) register_14 (.D(WD), .en(_25), .Q(_25out), .clk(clk), .clr(reset));
  Register #(.width(32)) register_15 (.D(WD), .en(_2), .Q(_2out), .clk(clk), .clr(reset));
  Register #(.width(32)) register_16 (.D(WD), .en(_9), .Q(_9out), .clk(clk), .clr(reset));
  Register #(.width(32)) register_17 (.D(WD), .en(_15), .Q(_15out), .clk(clk), .clr(reset));
  Register #(.width(32)) register_18 (.D(WD), .en(_21), .Q(_21out), .clk(clk), .clr(reset));
  Register #(.width(32)) register_19 (.D(WD), .en(_26), .Q(_26out), .clk(clk), .clr(reset));
  Register #(.width(32)) register_20 (.D(WD), .en(_4), .Q(_4out), .clk(clk), .clr(reset));
  Register #(.width(32)) register_21 (.D(WD), .en(_3), .Q(_3out), .clk(clk), .clr(reset));
  Register #(.width(32)) register_22 (.D(WD), .en(_11), .Q(_11out), .clk(clk), .clr(reset));
  Register #(.width(32)) register_23 (.D(WD), .en(_10), .Q(_10out), .clk(clk), .clr(reset));
  Register #(.width(32)) register_24 (.D(WD), .en(_17), .Q(_17out), .clk(clk), .clr(reset));
  Register #(.width(32)) register_25 (.D(WD), .en(_16), .Q(_16out), .clk(clk), .clr(reset));
  Register #(.width(32)) register_26 (.D(WD), .en(_22), .Q(_22out), .clk(clk), .clr(reset));
  Register #(.width(32)) register_27 (.D(WD), .en(_27), .Q(_27out), .clk(clk), .clr(reset));
  Register #(.width(32)) register_28 (.D(WD), .en(_28), .Q(_28out), .clk(clk), .clr(reset));
  Register #(.width(32)) register_29 (.D(WD), .en(_31), .Q(_31out), .clk(clk), .clr(reset));
  Register #(.width(32)) register_30 (.D(WD), .en(_5), .Q(_5out), .clk(clk), .clr(reset));
  Register #(.width(32)) register_31 (.D(WD), .en(_23), .Q(_23out), .clk(clk), .clr(reset));
  Register #(.width(32)) register_32 (.D(WD), .en(_29), .Q(_29out), .clk(clk), .clr(reset));
  Multiplexer #(.select(5), .width(32)) multiplexer_1 (
    .in0(_0out), .in1(_1out), .in2(_2out), .in3(_3out), .in4(_4out), .in5(_5out), .in6(_6out), .in7(_7out),
    .in8(_8out), .in9(_9out), .in10(_10out), .in11(_11out), .in12(_12out), .in13(_13out), .in14(_14out),
    .in15(_15out), .in16(_16out), .in17(_17out), .in18(_18out), .in19(_19out), .in20(_20out), .in21(_21out),
    .in22(_22out), .in23(_23out), .in24(_24out), .in25(_25out), .in26(_26out), .in27(_27out), .in28(_28out),
    .in29(_29out), .in30(_30out), .in31(_31out), .out(RD1), .sel(A1));  // open: en
  Multiplexer #(.select(5), .width(32)) multiplexer_2 (
    .in0(_0out), .in1(_1out), .in2(_2out), .in3(_3out), .in4(_4out), .in5(_5out), .in6(_6out), .in7(_7out),
    .in8(_8out), .in9(_9out), .in10(_10out), .in11(_11out), .in12(_12out), .in13(_13out), .in14(_14out),
    .in15(_15out), .in16(_16out), .in17(_17out), .in18(_18out), .in19(_19out), .in20(_20out), .in21(_21out),
    .in22(_22out), .in23(_23out), .in24(_24out), .in25(_25out), .in26(_26out), .in27(_27out), .in28(_28out),
    .in29(_29out), .in30(_30out), .in31(_31out), .out(RD2), .sel(A2));  // open: en

  // Other names for the same wires on the sheet: WE = \WE使能 
endmodule

module DM (
  input  [31:0] addr,
  input  DMwr,
  input  clk,
  input  [31:0] WD,
  input  reset,
  input  [1:0] DMop,
  output [31:0] RD
);

  wire [7:0] multiplexer_5_out, RD0_7, RD8_15, RD16_23, RD24_31;
  wire [15:0] multiplexer_4_out;
  wire [31:0] bit_extender_1_out, bit_extender_2_out, inData, multiplexer_1_out, multiplexer_2_out;

  Multiplexer #(.width(32)) multiplexer_1 (
    .in0({RD24_31, RD16_23, WD[15:0]}), .in1({WD[31:16], RD8_15, RD0_7}), .out(multiplexer_1_out),
    .sel(addr[1]));  // open: en
  Multiplexer #(.select(2), .width(32)) multiplexer_2 (
    .in0({RD24_31, RD16_23, RD8_15, WD[7:0]}), .in1({RD24_31, RD16_23, WD[15:8], RD0_7}),
    .in2({RD24_31, WD[23:16], RD8_15, RD0_7}), .in3({WD[31:24], RD16_23, RD8_15, RD0_7}),
    .out(multiplexer_2_out), .sel(addr[1:0]));  // open: en
  Multiplexer #(.select(2), .width(32)) multiplexer_3 (
    .in0(WD), .in1(multiplexer_1_out), .in2(multiplexer_2_out), .out(inData), .sel(DMop));  // open: in3, en
  RAM #(.addrWidth(12), .dataWidth(32), .bus("separate")) ram_1 (
    .addr(addr[13:2]), .din(inData), .data({RD24_31, RD16_23, RD8_15, RD0_7}), .str(DMwr), .clk(clk),
    .clr(reset));  // open: sel, ld
  // Probe on {RD24_31, RD16_23, RD8_15, RD0_7}
  Multiplexer #(.width(16)) multiplexer_4 (
    .in0({RD8_15, RD0_7}), .in1({RD24_31, RD16_23}), .out(multiplexer_4_out), .sel(addr[1]));  // open: en
  Multiplexer #(.select(2), .width(8)) multiplexer_5 (
    .in0(RD0_7), .in1(RD8_15), .in2(RD16_23), .in3(RD24_31), .out(multiplexer_5_out), .sel(addr[1:0]));  // open: en
  // Probe on {RD24_31, RD16_23, RD8_15, RD0_7}
  assign bit_extender_1_out = {{16{1'b0}}, multiplexer_4_out};  // Bit_Extender bit_extender_1
  assign bit_extender_2_out = {{24{1'b0}}, multiplexer_5_out};  // Bit_Extender bit_extender_2
  Multiplexer #(.select(2), .width(32)) multiplexer_6 (
    .in0({RD24_31, RD16_23, RD8_15, RD0_7}), .in1(bit_extender_1_out), .in2(bit_extender_2_out), .out(RD),
    .sel(DMop));  // open: in3, en
  // Probe on RD

  // Other names for the same wires on the sheet: WD0_7[7:0] = WD[7:0]; WD8_15[7:0] = WD[15:8];
  //   WD16_23[7:0] = WD[23:16]; WD24_31[7:0] = WD[31:24]; add[31:0] = addr
endmodule

module ALU (
  input  [3:0] ALUop,
  input  [31:0] A,
  input  [31:0] B,
  output Zero,
  output LessZero,
  output [31:0] C
);

  wire [31:0] adder_1_out, and_1_out, or_1_out, subtractor_1_out;

  Comparator #(.width(32)) comparator_1 (.a(A), .b(B), .eq(Zero), .lt(LessZero));  // open: gt
  Adder #(.width(32)) adder_1 (.a(A), .b(B), .out(adder_1_out));  // open: cin, cout
  Subtractor #(.width(32)) subtractor_1 (.a(A), .b(B), .out(subtractor_1_out));  // open: bin, bout
  assign or_1_out = A | B;  // OR_Gate or_1, 32 bits wide
  assign and_1_out = B & B;  // AND_Gate and_1, 32 bits wide
  Multiplexer #(.select(4), .width(32)) multiplexer_1 (
    .in0(adder_1_out), .in1(subtractor_1_out), .in2(or_1_out), .in3({B[15:0], {16{1'b0}}}), .in4(and_1_out),
    .out(C), .sel(ALUop));  // open: in5, in6, in7, in8, in9, in10, in11, in12, in13, in14, in15, en
endmodule

module EXT (
  input  [15:0] Imm,
  input  EXTop,
  output [31:0] extOut
);

  wire [31:0] bit_extender_1_out, bit_extender_2_out;

  assign bit_extender_1_out = {{16{1'b0}}, Imm};  // Bit_Extender bit_extender_1
  assign bit_extender_2_out = {{16{Imm[15]}}, Imm};  // Bit_Extender bit_extender_2
  Multiplexer #(.width(32)) multiplexer_1 (
    .in0(bit_extender_1_out), .in1(bit_extender_2_out), .out(extOut), .sel(EXTop));  // open: en
endmodule

module Splitter (
  input  [31:0] Code,
  output [5:0] funct,
  output [4:0] _15_11,
  output [4:0] _20_16,
  output [4:0] _25_21,
  output [5:0] opcode,
  output [25:0] Imm26,
  output [15:0] Imm16
);


  assign _15_11 = Code[15:11];
  assign _20_16 = Code[20:16];
  assign _25_21 = Code[25:21];
  assign funct = Code[5:0];
  assign Imm16 = Code[15:0];
  assign Imm26 = Code[25:0];
  assign opcode = Code[31:26];
endmodule
